# Fritzing sketch camera_capture_with_button (saved by Fritzing 0.9.3b)
breadboards: 1

parts:
  Raspberry_Pi_1 = Raspberry Pi 3 [part_number=RPI-3-V1.2]
  S1 = Pushbutton [package="[THT]"]
  R2 = Resistor [tolerance=±5% resistance=10k package=THT]
  CAMERA1 = TTL Serial JPEG Camera  # not connected

nets:
  N1: Raspberry_Pi_1.3v3, R2.Pin_0
  N2: Raspberry_Pi_1.GND, S1.Pin_1, S1.Pin_2
  N3: Raspberry_Pi_1.GPIO25, S1.Pin_3, S1.Pin_4, R2.Pin_1

notes:
  Raspberry Pi Camera Module v2

custom parts:
  TTL Serial JPEG Camera: TTL Serial JPEG Camera with NTSC Out
