# Fritzing sketch device_screen_auto_tapping (saved by Fritzing 0.9.3b)

parts:
  Raspberry_Pi_1 = Raspberry Pi 3 [part_number=RPI-3-V1.2]
  IC1 = G6L-1F [chip_label=IC package="DIP (Dual Inline) [THT]"]

nets:
  N1: Raspberry_Pi_1.GPIO18, IC1.pin3
  N2: Raspberry_Pi_1.GND, IC1.pin2
  N3: Raspberry_Pi_1.5V, IC1.pin1

custom parts:
  G6L-1F: A DIP stand-in part for whatever IC you want. With 8 pins on a 300mil dual inline package (DIP) footprint.
